// Logisim project cpu.circ as structural Verilog: 15 circuits, main circuit Full adder
module Main (
  input  Reset,
  output NULL
);

  wire Clock_out, controle_unit_1_fetch, controle_unit_1_wad, controle_unit_1_wpc;
  wire [1:0] controle_unit_1_readx, controle_unit_1_ready, controle_unit_1_write_2;
  wire [2:0] controle_unit_1_alu;
  wire [3:0] adressing_unit_1_ad_out, adressing_unit_1_pc_out, controle_unit_1_ad_out, controle_unit_1_pcout,
       registers_bench_1_x, registers_bench_1_y, rom_1_data;
  wire [11:0] ram_1_data;

  ROM #(.addrWidth(4), .dataWidth(4)) rom_1 (.addr(adressing_unit_1_ad_out), .data(rom_1_data));  // open: sel
  RAM #(.addrWidth(4), .dataWidth(12)) ram_1 (
    .addr(adressing_unit_1_pc_out), .data(ram_1_data), .clk(Clock_out));  // open: sel, ld, clr
  Controle_unit controle_unit_1 (
    .InstructionIn(ram_1_data), .ALU(controle_unit_1_alu), .Clock(Clock_out), .Reset(Reset),
    .wAD(controle_unit_1_wad), .wPC(controle_unit_1_wpc), .Fetch(controle_unit_1_fetch),
    .write_2(controle_unit_1_write_2), .ReadX(controle_unit_1_readx), .ReadY(controle_unit_1_ready),
    .PcIn(adressing_unit_1_pc_out), .PcOut(controle_unit_1_pcout), .AD_out(controle_unit_1_ad_out));  // open: Read, write, ext1, ext2
  Adressing_unit adressing_unit_1 (
    .PC_in(controle_unit_1_pcout), .AD_in(controle_unit_1_ad_out), .PC_out(adressing_unit_1_pc_out),
    .AD_out(adressing_unit_1_ad_out), .wrPC(controle_unit_1_wpc), .wrAD(controle_unit_1_wad),
    .clock(Clock_out), .Reset(Reset));
  Registers_Bench registers_bench_1 (
    .Clock(Clock_out), .Input(rom_1_data), .Write(controle_unit_1_write_2), .Read_Y(controle_unit_1_ready),
    .Read_X(controle_unit_1_readx), .Reset(Reset), .X(registers_bench_1_x), .Y(registers_bench_1_y));
  LED Fetch (.in(controle_unit_1_fetch));
  Clock Clock (.out(Clock_out));
  ALU_4bits alu_4bits_1 (
    .X(registers_bench_1_x), .Y(registers_bench_1_y), .out(rom_1_data), .Sel(controle_unit_1_alu),
    .NULL(NULL), .c_in(1'b0));  // open: c_out_add, c_out_sub

  // Notes on the sheet:
  //   Mémoire de données
  //   Mémoire d'instructions
endmodule

module Full_adder (
  input  Cin,
  input  X,
  input  Y,
  output Somme,
  output Cout
);

  wire and_1_out, and_2_out, xor_1_out;

  and and_1 (and_1_out, X, Y);
  xor xor_1 (xor_1_out, X, Y);
  or or_1 (Cout, and_1_out, and_2_out);
  and and_2 (and_2_out, xor_1_out, Cin);
  xor xor_2 (Somme, Cin, xor_1_out);
endmodule

module Full_substractor (
  input  Cin,
  input  X,
  input  Y,
  output substraction_x_y,
  output Cout
);

  wire and_1_out, and_2_out, not_1_out, not_2_out, xor_1_out;

  not not_1 (not_1_out, X);
  and and_1 (and_1_out, not_1_out, Y);
  xor xor_1 (xor_1_out, X, Y);
  or or_1 (Cout, and_1_out, and_2_out);
  not not_2 (not_2_out, xor_1_out);
  and and_2 (and_2_out, not_2_out, Cin);
  xor xor_2 (substraction_x_y, Cin, xor_1_out);
endmodule

module Multiplexer_2to1 (
  input  in_1,
  input  in_2,
  input  SEL,
  output out_4
);

  wire and_1_out, and_2_out, not_1_out;

  not not_1 (not_1_out, SEL);
  and and_1 (and_1_out, in_1, SEL);
  and and_2 (and_2_out, in_2, not_1_out);
  or or_1 (out_4, and_1_out, and_2_out);
endmodule

// DEC
module Decoder_2bits (
  input  [1:0] Input,
  output S0,
  output S1,
  output S2,
  output S3
);

  wire not_1_out, not_2_out;

  not not_1 (not_1_out, Input[1]);
  not not_2 (not_2_out, Input[0]);
  and and_1 (S0, not_1_out, not_2_out);
  and and_2 (S1, not_1_out, Input[0]);
  and and_3 (S2, Input[1], not_2_out);
  and and_4 (S3, Input[1], Input[0]);
endmodule

// DEC
module Decoder_3bits (
  input  [2:0] \input ,
  output s0,
  output s1,
  output s2,
  output s3,
  output s4,
  output s5,
  output s6,
  output s7
);

  wire not_1_out, not_2_out, not_3_out;

  not not_1 (not_1_out, \input [2]);
  not not_2 (not_2_out, \input [1]);
  not not_3 (not_3_out, \input [0]);
  and and_1 (s0, not_2_out, not_3_out, not_1_out);
  and and_2 (s1, not_2_out, \input [0], not_1_out);
  and and_3 (s2, \input [1], not_3_out, not_1_out);
  and and_4 (s3, \input [1], \input [0], not_1_out);
  and and_5 (s4, not_2_out, not_3_out, \input [2]);
  and and_6 (s5, \input [2], \input [0], not_2_out);
  and and_7 (s6, \input [2], not_3_out, \input [1]);
  and and_8 (s7, \input [2], \input [0], \input [1]);
endmodule

module Incrementer_4bits (
  input  e3,
  input  e2,
  input  e1,
  input  e0,
  output Se3,
  output Se2,
  output Se1,
  output Se0
);

  wire and_1_out, and_2_out, and_3_out, and_4_out, and_5_out, and_6_out, and_7_out, and_8_out, and_9_out,
       not_1_out, not_2_out, not_3_out, not_4_out, not_5_out, not_6_out, not_7_out, not_8_out, not_9_out;

  not not_1 (not_1_out, e3);
  not not_2 (not_2_out, e2);
  not not_3 (not_3_out, e1);
  not not_4 (not_4_out, e0);
  not not_5 (not_5_out, e2);
  not not_6 (not_6_out, e1);
  not not_7 (not_7_out, e0);
  not not_8 (not_8_out, e1);
  not not_9 (not_9_out, e0);
  not not_10 (Se0, e0);
  and and_1 (and_1_out, not_1_out, e2, e1, e0);
  and and_2 (and_2_out, e3, not_2_out);
  and and_3 (and_3_out, e3, not_3_out);
  and and_4 (and_4_out, e3, not_4_out);
  and and_5 (and_5_out, not_5_out, e1, e0);
  and and_6 (and_6_out, e2, not_6_out);
  and and_7 (and_7_out, e2, not_7_out);
  and and_8 (and_8_out, not_8_out, e0);
  and and_9 (and_9_out, e1, not_9_out);
  or or_1 (Se3, and_1_out, and_2_out, and_3_out, and_4_out);
  or or_2 (Se2, and_5_out, and_6_out, and_7_out);
  or or_3 (Se1, and_8_out, and_9_out);
endmodule

module ALU_1bit (
  input  Cin_add,
  input  X,
  input  Y,
  input  Cin_sub,
  input  [2:0] select,
  output Cout_add,
  output Sortie,
  output cout_sub,
  output NULL
);

  wire and_1_out, and_2_out, and_3_out, and_4_out, and_5_out, and_6_out, and_7_out, and_8_out, and_9_out,
       decoder_3bits_1_s0, decoder_3bits_1_s1, decoder_3bits_1_s2, decoder_3bits_1_s3, decoder_3bits_1_s4,
       decoder_3bits_1_s5, decoder_3bits_1_s6, decoder_3bits_1_s7, full_adder_1_somme,
       full_substractor_1_substraction_x_y, nand_1_out, nor_1_out, not_1_out, not_2_out, not_3_out,
       not_4_out, not_5_out, not_6_out, not_7_out, not_8_out, not_9_out, or_1_out, xor_1_out;

  Full_adder full_adder_1 (.X(X), .Y(Y), .Cin(Cin_add), .Somme(full_adder_1_somme), .Cout(Cout_add));
  or or_1 (or_1_out, X, Y);
  not not_1 (not_1_out, X);
  and and_1 (and_1_out, X, Y);
  xor xor_1 (xor_1_out, X, Y);
  nand nand_1 (nand_1_out, X, Y);
  nor nor_1 (nor_1_out, X, Y);
  Full_substractor full_substractor_1 (
    .X(X), .Y(Y), .Cin(Cin_sub), .Cout(cout_sub), .substraction_x_y(full_substractor_1_substraction_x_y));
  Decoder_3bits decoder_3bits_1 (
    .s0(decoder_3bits_1_s0), .s1(decoder_3bits_1_s1), .s2(decoder_3bits_1_s2), .s3(decoder_3bits_1_s3),
    .s4(decoder_3bits_1_s4), .s5(decoder_3bits_1_s5), .s6(decoder_3bits_1_s6), .s7(decoder_3bits_1_s7),
    .\input (select));
  and and_2 (and_2_out, full_adder_1_somme, decoder_3bits_1_s0);
  and and_3 (and_3_out, decoder_3bits_1_s1, full_substractor_1_substraction_x_y);
  and and_4 (and_4_out, decoder_3bits_1_s2, or_1_out);
  and and_5 (and_5_out, not_1_out, decoder_3bits_1_s3);
  and and_6 (and_6_out, and_1_out, decoder_3bits_1_s4);
  and and_7 (and_7_out, xor_1_out, decoder_3bits_1_s5);
  and and_8 (and_8_out, nand_1_out, decoder_3bits_1_s6);
  and and_9 (and_9_out, nor_1_out, decoder_3bits_1_s7);
  not not_2 (not_2_out, and_9_out);
  not not_3 (not_3_out, and_6_out);
  not not_4 (not_4_out, and_7_out);
  not not_5 (not_5_out, and_2_out);
  not not_6 (not_6_out, and_5_out);
  not not_7 (not_7_out, and_8_out);
  not not_8 (not_8_out, and_4_out);
  not not_9 (not_9_out, and_3_out);
  and and_10 (NULL, not_2_out, not_7_out, not_4_out, not_3_out, not_6_out, not_8_out, not_9_out, not_5_out);
  or or_2 (Sortie, and_2_out, and_3_out, and_4_out, and_5_out, and_6_out, and_7_out, and_8_out, and_9_out);
endmodule

module ALU_4bits (
  input  c_in,
  input  [3:0] X,
  input  [3:0] Y,
  input  [2:0] Sel,
  output [3:0] out,
  output c_out_sub,
  output NULL,
  output c_out_add
);

  wire alu_1bit_1_cout_add, alu_1bit_1_cout_sub, alu_1bit_1_null, alu_1bit_2_cout_add, alu_1bit_2_cout_sub,
       alu_1bit_2_null, alu_1bit_3_cout_add, alu_1bit_3_cout_sub, alu_1bit_3_null, alu_1bit_4_null;

  ALU_1bit alu_1bit_1 (
    .Y(Y[0]), .Sortie(out[0]), .Cin_add(c_in), .Cout_add(alu_1bit_1_cout_add), .X(X[0]), .select(Sel),
    .NULL(alu_1bit_1_null), .cout_sub(alu_1bit_1_cout_sub), .Cin_sub(c_in));
  ALU_1bit alu_1bit_2 (
    .Y(Y[1]), .Sortie(out[1]), .Cin_add(alu_1bit_1_cout_add), .Cout_add(alu_1bit_2_cout_add), .X(X[1]),
    .select(Sel), .NULL(alu_1bit_2_null), .cout_sub(alu_1bit_2_cout_sub), .Cin_sub(alu_1bit_1_cout_sub));
  ALU_1bit alu_1bit_3 (
    .Y(Y[2]), .Sortie(out[2]), .Cin_add(alu_1bit_2_cout_add), .Cout_add(alu_1bit_3_cout_add), .X(X[2]),
    .select(Sel), .NULL(alu_1bit_3_null), .cout_sub(alu_1bit_3_cout_sub), .Cin_sub(alu_1bit_2_cout_sub));
  ALU_1bit alu_1bit_4 (
    .Y(Y[3]), .Sortie(out[3]), .Cin_add(alu_1bit_3_cout_add), .Cout_add(c_out_add), .X(X[3]), .select(Sel),
    .NULL(alu_1bit_4_null), .cout_sub(c_out_sub), .Cin_sub(alu_1bit_3_cout_sub));
  and and_1 (NULL, alu_1bit_1_null, alu_1bit_2_null, alu_1bit_3_null, alu_1bit_4_null);
endmodule

// REG 4b
module Registrer_4bits (
  input  [3:0] \input ,
  input  write,
  input  Clock,
  input  Reset,
  input  Read_X,
  input  Read_Y,
  output [3:0] X,
  output [3:0] Y
);

  wire controlled_buffer_1_out, controlled_buffer_3_out, controlled_buffer_5_out, controlled_buffer_6_out,
       d_ff_1_q, d_ff_2_q, d_ff_3_q, d_ff_4_q;

  assign controlled_buffer_1_out = write ? \input [3] : 1'bz;  // Controlled_Buffer controlled_buffer_1
  D_Flip_Flop d_ff_1 (.clk(Clock), .D(controlled_buffer_1_out), .Q(d_ff_1_q), .reset(Reset));  // open: Qn, preset, en
  assign X[3] = Read_X ? d_ff_1_q : 1'bz;  // Controlled_Buffer controlled_buffer_2
  assign controlled_buffer_3_out = write ? \input [2] : 1'bz;  // Controlled_Buffer controlled_buffer_3
  D_Flip_Flop d_ff_2 (.clk(Clock), .D(controlled_buffer_3_out), .Q(d_ff_2_q), .reset(Reset));  // open: Qn, preset, en
  assign X[2] = Read_X ? d_ff_2_q : 1'bz;  // Controlled_Buffer controlled_buffer_4
  assign controlled_buffer_5_out = write ? \input [1] : 1'bz;  // Controlled_Buffer controlled_buffer_5
  D_Flip_Flop d_ff_3 (.clk(Clock), .D(controlled_buffer_5_out), .Q(d_ff_3_q), .reset(Reset));  // open: Qn, preset, en
  assign controlled_buffer_6_out = write ? \input [0] : 1'bz;  // Controlled_Buffer controlled_buffer_6
  assign X[1] = Read_X ? d_ff_3_q : 1'bz;  // Controlled_Buffer controlled_buffer_7
  D_Flip_Flop d_ff_4 (.clk(Clock), .D(controlled_buffer_6_out), .Q(d_ff_4_q), .reset(Reset));  // open: Qn, preset, en
  assign X[0] = Read_X ? d_ff_4_q : 1'bz;  // Controlled_Buffer controlled_buffer_8
  assign Y[3] = Read_Y ? d_ff_1_q : 1'bz;  // Controlled_Buffer controlled_buffer_9
  assign Y[2] = Read_Y ? d_ff_2_q : 1'bz;  // Controlled_Buffer controlled_buffer_10
  assign Y[1] = Read_Y ? d_ff_3_q : 1'bz;  // Controlled_Buffer controlled_buffer_11
  assign Y[0] = Read_Y ? d_ff_4_q : 1'bz;  // Controlled_Buffer controlled_buffer_12
endmodule

module Registers_Bench (
  input  Clock,
  input  Reset,
  input  [3:0] Input,
  input  [1:0] Write,
  input  [1:0] Read_Y,
  input  [1:0] Read_X,
  output [3:0] X,
  output [3:0] Y
);

  wire decoder_2bits_1_s0, decoder_2bits_1_s1, decoder_2bits_1_s2, decoder_2bits_1_s3, decoder_2bits_2_s0,
       decoder_2bits_2_s1, decoder_2bits_2_s2, decoder_2bits_2_s3, decoder_2bits_3_s0, decoder_2bits_3_s1,
       decoder_2bits_3_s2, decoder_2bits_3_s3;

  Decoder_2bits decoder_2bits_1 (
    .Input(Write), .S0(decoder_2bits_1_s0), .S1(decoder_2bits_1_s1), .S2(decoder_2bits_1_s2),
    .S3(decoder_2bits_1_s3));
  Decoder_2bits decoder_2bits_2 (
    .Input(Read_Y), .S0(decoder_2bits_2_s0), .S1(decoder_2bits_2_s1), .S2(decoder_2bits_2_s2),
    .S3(decoder_2bits_2_s3));
  Decoder_2bits decoder_2bits_3 (
    .Input(Read_X), .S0(decoder_2bits_3_s0), .S1(decoder_2bits_3_s1), .S2(decoder_2bits_3_s2),
    .S3(decoder_2bits_3_s3));
  Registrer_4bits registrer_4bits_1 (
    .\input (Input), .write(decoder_2bits_1_s3), .Clock(Clock), .Reset(Reset), .Read_X(decoder_2bits_3_s3),
    .Read_Y(decoder_2bits_2_s3), .Y(Y), .X(X));
  Registrer_4bits registrer_4bits_2 (
    .\input (Input), .write(decoder_2bits_1_s2), .Clock(Clock), .Reset(Reset), .Read_X(decoder_2bits_3_s2),
    .Read_Y(decoder_2bits_2_s2), .Y(Y), .X(X));
  Registrer_4bits registrer_4bits_3 (
    .\input (Input), .write(decoder_2bits_1_s1), .Clock(Clock), .Reset(Reset), .Read_X(decoder_2bits_3_s1),
    .Read_Y(decoder_2bits_2_s1), .Y(Y), .X(X));
  Registrer_4bits registrer_4bits_4 (
    .\input (Input), .write(decoder_2bits_1_s0), .Clock(Clock), .Reset(Reset), .Read_X(decoder_2bits_3_s0),
    .Read_Y(decoder_2bits_2_s0), .Y(Y), .X(X));
endmodule

module Adressing_unit (
  input  Reset,
  input  [3:0] PC_in,
  input  wrPC,
  input  clock,
  input  [3:0] AD_in,
  input  wrAD,
  output [3:0] PC_out,
  output [3:0] AD_out
);

  Registrer_4bits PC (
    .\input (PC_in), .write(wrPC), .Clock(clock), .Reset(Reset), .Read_X(1'b1), .Read_Y(1'b0), .X(PC_out));  // open: Y
  Registrer_4bits AD (
    .\input (AD_in), .write(wrAD), .Clock(clock), .Reset(Reset), .Read_X(1'b1), .Read_Y(1'b0), .X(AD_out));  // open: Y
endmodule

// RI
module Instructions_Register (
  input  [11:0] Input,
  input  read,
  input  write,
  input  CLK,
  input  Reset,
  output [11:0] \output 
);

  wire controlled_buffer_1_out, controlled_buffer_2_out, controlled_buffer_3_out, controlled_buffer_4_out,
       controlled_buffer_5_out, controlled_buffer_6_out, controlled_buffer_7_out, controlled_buffer_8_out,
       controlled_buffer_9_out, controlled_buffer_10_out, controlled_buffer_11_out, controlled_buffer_12_out,
       d_ff_1_q, d_ff_2_q, d_ff_3_q, d_ff_4_q, d_ff_5_q, d_ff_6_q, d_ff_7_q, d_ff_8_q, d_ff_9_q, d_ff_10_q,
       d_ff_11_q, d_ff_12_q;

  assign controlled_buffer_1_out = write ? Input[0] : 1'bz;  // Controlled_Buffer controlled_buffer_1
  assign controlled_buffer_2_out = write ? Input[1] : 1'bz;  // Controlled_Buffer controlled_buffer_2
  assign controlled_buffer_3_out = write ? Input[2] : 1'bz;  // Controlled_Buffer controlled_buffer_3
  assign controlled_buffer_4_out = write ? Input[3] : 1'bz;  // Controlled_Buffer controlled_buffer_4
  assign controlled_buffer_5_out = write ? Input[4] : 1'bz;  // Controlled_Buffer controlled_buffer_5
  assign controlled_buffer_6_out = write ? Input[5] : 1'bz;  // Controlled_Buffer controlled_buffer_6
  assign controlled_buffer_7_out = write ? Input[6] : 1'bz;  // Controlled_Buffer controlled_buffer_7
  assign controlled_buffer_8_out = write ? Input[7] : 1'bz;  // Controlled_Buffer controlled_buffer_8
  assign controlled_buffer_9_out = write ? Input[8] : 1'bz;  // Controlled_Buffer controlled_buffer_9
  assign controlled_buffer_10_out = write ? Input[9] : 1'bz;  // Controlled_Buffer controlled_buffer_10
  assign controlled_buffer_11_out = write ? Input[10] : 1'bz;  // Controlled_Buffer controlled_buffer_11
  assign controlled_buffer_12_out = write ? Input[11] : 1'bz;  // Controlled_Buffer controlled_buffer_12
  D_Flip_Flop d_ff_1 (.clk(CLK), .D(controlled_buffer_1_out), .Q(d_ff_1_q), .reset(Reset));  // open: Qn, preset, en
  D_Flip_Flop d_ff_2 (.clk(CLK), .D(controlled_buffer_2_out), .Q(d_ff_2_q), .reset(Reset));  // open: Qn, preset, en
  D_Flip_Flop d_ff_3 (.clk(CLK), .D(controlled_buffer_3_out), .Q(d_ff_3_q), .reset(Reset));  // open: Qn, preset, en
  D_Flip_Flop d_ff_4 (.clk(CLK), .D(controlled_buffer_4_out), .Q(d_ff_4_q), .reset(Reset));  // open: Qn, preset, en
  D_Flip_Flop d_ff_5 (.clk(CLK), .D(controlled_buffer_5_out), .Q(d_ff_5_q), .reset(Reset));  // open: Qn, preset, en
  D_Flip_Flop d_ff_6 (.clk(CLK), .D(controlled_buffer_6_out), .Q(d_ff_6_q), .reset(Reset));  // open: Qn, preset, en
  D_Flip_Flop d_ff_7 (.clk(CLK), .D(controlled_buffer_7_out), .Q(d_ff_7_q), .reset(Reset));  // open: Qn, preset, en
  D_Flip_Flop d_ff_8 (.clk(CLK), .D(controlled_buffer_8_out), .Q(d_ff_8_q), .reset(Reset));  // open: Qn, preset, en
  D_Flip_Flop d_ff_9 (.clk(CLK), .D(controlled_buffer_9_out), .Q(d_ff_9_q), .reset(Reset));  // open: Qn, preset, en
  D_Flip_Flop d_ff_10 (.clk(CLK), .D(controlled_buffer_10_out), .Q(d_ff_10_q), .reset(Reset));  // open: Qn, preset, en
  D_Flip_Flop d_ff_11 (.clk(CLK), .D(controlled_buffer_11_out), .Q(d_ff_11_q), .reset(Reset));  // open: Qn, preset, en
  D_Flip_Flop d_ff_12 (.clk(CLK), .D(controlled_buffer_12_out), .Q(d_ff_12_q), .reset(Reset));  // open: Qn, preset, en
  assign \output [0] = read ? d_ff_1_q : 1'bz;  // Controlled_Buffer controlled_buffer_13
  assign \output [1] = read ? d_ff_2_q : 1'bz;  // Controlled_Buffer controlled_buffer_14
  assign \output [2] = read ? d_ff_3_q : 1'bz;  // Controlled_Buffer controlled_buffer_15
  assign \output [3] = read ? d_ff_4_q : 1'bz;  // Controlled_Buffer controlled_buffer_16
  assign \output [4] = read ? d_ff_5_q : 1'bz;  // Controlled_Buffer controlled_buffer_17
  assign \output [5] = read ? d_ff_6_q : 1'bz;  // Controlled_Buffer controlled_buffer_18
  assign \output [6] = read ? d_ff_7_q : 1'bz;  // Controlled_Buffer controlled_buffer_19
  assign \output [7] = read ? d_ff_8_q : 1'bz;  // Controlled_Buffer controlled_buffer_20
  assign \output [8] = read ? d_ff_9_q : 1'bz;  // Controlled_Buffer controlled_buffer_21
  assign \output [9] = read ? d_ff_10_q : 1'bz;  // Controlled_Buffer controlled_buffer_22
  assign \output [10] = read ? d_ff_11_q : 1'bz;  // Controlled_Buffer controlled_buffer_23
  assign \output [11] = read ? d_ff_12_q : 1'bz;  // Controlled_Buffer controlled_buffer_24
endmodule

module Instructions_decoder (
  input  [3:0] OpCod,
  output f0,
  output f1,
  output f2,
  output R,
  output W,
  output wAD,
  output wPC,
  output Fetch
);

  wire and_1_out, and_2_out, and_3_out, and_4_out, and_5_out, and_6_out, not_1_out, not_2_out, not_3_out,
       not_4_out, not_5_out, not_6_out, not_7_out, not_8_out, not_9_out, not_10_out, not_11_out, not_12_out,
       not_13_out, not_14_out, or_1_out, or_2_out, or_4_out, xor_1_out;

  not not_1 (not_1_out, OpCod[2]);
  not not_2 (not_2_out, OpCod[3]);
  not not_3 (not_3_out, OpCod[0]);
  not not_4 (not_4_out, OpCod[2]);
  not not_5 (not_5_out, OpCod[3]);
  not not_6 (not_6_out, OpCod[0]);
  not not_7 (not_7_out, OpCod[2]);
  not not_8 (not_8_out, OpCod[3]);
  not not_9 (not_9_out, OpCod[0]);
  not not_10 (not_10_out, OpCod[2]);
  not not_11 (not_11_out, OpCod[0]);
  not not_12 (not_12_out, OpCod[1]);
  not not_13 (not_13_out, OpCod[2]);
  not not_14 (not_14_out, OpCod[3]);
  and and_1 (and_1_out, OpCod[0], not_1_out, not_2_out);
  xor xor_1 (xor_1_out, OpCod[2], OpCod[3]);
  or or_1 (or_1_out, OpCod[0], not_4_out);
  or or_2 (or_2_out, OpCod[0], OpCod[1]);
  and and_2 (and_2_out, not_3_out, OpCod[1], xor_1_out);
  and and_3 (and_3_out, or_1_out, not_5_out);
  and and_4 (and_4_out, not_6_out, not_7_out, OpCod[3]);
  and and_5 (and_5_out, not_8_out, OpCod[2], or_2_out);
  and and_6 (and_6_out, not_9_out, OpCod[1], not_10_out, OpCod[3]);
  or or_3 (f0, and_1_out, and_2_out);
  and and_7 (f1, OpCod[1], or_4_out);
  or or_4 (or_4_out, and_3_out, and_4_out);
  or or_5 (f2, and_5_out, and_6_out);
  and and_8 (R, not_11_out, not_12_out, OpCod[2], not_14_out);
  and and_9 (W, not_11_out, not_12_out, not_13_out, OpCod[3]);
  or or_6 (wAD, R, W);

  assign Fetch = 1'b1;
  assign wPC = 1'b1;
endmodule

module Controle_unit (
  input  [3:0] PcIn,
  input  [11:0] InstructionIn,
  input  Clock,
  input  Reset,
  output [2:0] ALU,
  output Read,
  output write,
  output [3:0] PcOut,
  output wAD,
  output wPC,
  output Fetch,
  output [1:0] write_2,
  output [1:0] ReadX,
  output [1:0] ReadY,
  output [3:0] AD_out,
  output ext1,
  output ext2
);

  wire [11:8] instructions_register_1_output;

  Instructions_Register instructions_register_1 (
    .\output ({instructions_register_1_output, write_2[0], write_2[1], AD_out, ext2, ext1}),
    .Input(InstructionIn), .write(1'b1), .read(1'b1), .CLK(Clock), .Reset(Reset));
  Incrementer_4bits incrementer_4bits_1 (
    .e3(PcIn[0]), .e2(PcIn[1]), .e1(PcIn[2]), .e0(PcIn[3]), .Se3(PcOut[0]), .Se2(PcOut[1]), .Se1(PcOut[2]),
    .Se0(PcOut[3]));
  Instructions_decoder instructions_decoder_1 (
    .OpCod(instructions_register_1_output), .R(Read), .W(write), .wAD(wAD), .wPC(wPC), .Fetch(Fetch),
    .f0(ALU[0]), .f1(ALU[1]), .f2(ALU[2]));

  assign ReadX = {AD_out[2], AD_out[3]};
  assign ReadY = {AD_out[0], AD_out[1]};
endmodule
